# Fritzing sketch TheMask (saved by Fritzing 0.9.3b)

parts:
  Matrix = WS2812 RGB LED matrix 8x8
  R1 = Resistor [tolerance=±5% resistance=330 package=THT]
  Microphone = Breakout Board for Electret Microphone
  Arduino = Arduino Nano (Rev3.0)
  Button = Pushbutton [package="[THT]"]

nets:
  GND: Matrix.GND, Microphone.GND, Arduino.GND, Button.Pin_3, Button.Pin_4
  VCC: Matrix.VCC, Microphone.VCC, Arduino.VIN
  N1: Matrix.DIN, R1.Pin_0
  N2: R1.Pin_1, Arduino.D7
  N3: Microphone.AUD, Arduino.A7
  N4: Arduino.D2, Button.Pin_1, Button.Pin_2

custom parts:
  WS2812 RGB LED matrix 8x8: WS2812 matrix 8x8
